# Fritzing sketch schematic (saved by Fritzing 0.9.3b)
breadboards: 1

parts:
  U1 = NodeMCU V3.0
  Componente1 = Arduino Uno (Rev3)
  R1 = Resistor [tolerance=±5% resistance=1k package="0603 [SMD]"]
  R2 = Resistor [tolerance=±5% resistance=470 package="0603 [SMD]"]
  JP1 = RCA [package=rca]

nets:
  N1: U1.D1, Componente1.D2
  N2: U1.D2, Componente1.D3_PWM
  N3: U1.D3, Componente1.D4
  N4: U1.GND#6, U1.GND#13, U1.GND#16, U1.GND#33, Componente1.GND, JP1.SHELL
  VIN: U1.Vin, Componente1.VIN
  N5: Componente1.D9_PWM, R1.Pin_0
  N6: Componente1.D7, R2.Pin_1
  N7: R1.Pin_1, R2.Pin_0, JP1.PIN

custom parts:
  NodeMCU V3.0: ESP8266 based NodeMCU
